# Fritzing sketch 01_LED (saved by Fritzing 0.9.2b)
breadboards: 1

parts:
  R1 = Resistor [tolerance=±5% resistance=10k package=THT]
  R2 = Resistor [tolerance=±5% resistance=220 package=THT]
  LED1 = LED - 5mm [color="Red (633nm)" package="5 mm [THT]"]
  Arduino_Uno = Arduino Uno (Rev3)
  S1 = Pushbutton [package="[THT]"]

nets:
  GND: R1.Pin_0, R2.Pin_1
  N1: R1.Pin_1, Arduino_Uno.D2, S1.Pin_1, S1.Pin_2
  N2: R2.Pin_0, LED1.cathode
  N3: LED1.anode, Arduino_Uno.D11_PWM/MOSI
  5V: S1.Pin_3
