# Fritzing sketch 02_TrafficLight (saved by Fritzing 0.9.2b)
breadboards: 1

parts:
  Arduino_Uno = Arduino Uno (Rev3)
  LED1 = LED - 5mm [color="Red (633nm)" package="5 mm [THT]"]
  R1 = Resistor [tolerance=±5% resistance=220 package=THT]
  LED2 = LED - 5mm [color="Yellow (574nm)" package="5 mm [THT]"]
  R2 = Resistor [tolerance=±5% resistance=220 package=THT]
  LED4 = LED - 5mm [color="Green (555nm)" package="5 mm [THT]"]
  R4 = Resistor [tolerance=±5% resistance=220 package=THT]

nets:
  N1: Arduino_Uno.D4, LED4.anode
  N2: Arduino_Uno.D5_PWM, LED2.anode
  N3: Arduino_Uno.D6_PWM, LED1.anode
  N4: LED1.cathode, R1.Pin_0
  GND: R1.Pin_1, R2.Pin_1, R4.Pin_1
  N5: LED2.cathode, R2.Pin_0
  N6: LED4.cathode, R4.Pin_0
