# Fritzing sketch 03_Photocell (saved by Fritzing 0.9.2b)
breadboards: 1

parts:
  Photocell = Photocell (LDR) [package=THT]
  R2 = Resistor [tolerance=±5% resistance=10k package=THT]
  Arduino_Uno = Arduino Uno (Rev3)

nets:
  N1: Photocell.pin_0, R2.Pin_0, Arduino_Uno.A0
  N2: Photocell.pin_1, Arduino_Uno.5V
  N3: R2.Pin_1, Arduino_Uno.GND
