# Fritzing sketch 04_Tilt_Switch (saved by Fritzing 0.9.2b)
breadboards: 1

parts:
  아두이노_우노 = Arduino Uno (Rev3)
  R1 = Resistor [tolerance=±5% resistance=220 package="0402 [SMD]"]
  LED1 = LED - 3mm [color="Red (633nm)" package="3 mm [THT]"]
  S1 = Tilt Switch [package=THT]

nets:
  N1: 아두이노_우노.D12/MISO, S1.Pin_1
  N2: 아두이노_우노.GND, R1.Pin_1, S1.Pin_2
  N3: 아두이노_우노.D2, LED1.anode
  N4: R1.Pin_0, LED1.cathode
