# Fritzing sketch 05_IPS (saved by Fritzing 0.9.2b)
breadboards: 1

parts:
  아두이노_우노 = Arduino Uno (Rev3)
  Ultrasonic_Sensor = HC-SR04

nets:
  N1: 아두이노_우노.D8, Ultrasonic_Sensor.Trig
  N2: 아두이노_우노.D9_PWM, Ultrasonic_Sensor.Echo
  GND: 아두이노_우노.GND, Ultrasonic_Sensor.GND
  5V: 아두이노_우노.5V, Ultrasonic_Sensor.VCC

custom parts:
  HC-SR04: Ultrasonic Sensor
