# Fritzing sketch 06_74HC595_Shift_Register (saved by Fritzing 0.9.2b)
breadboards: 1

parts:
  Arduino_Uno = Arduino Uno (Rev3)
  R1 = Resistor [tolerance=±5% resistance=220 package="0603 [SMD]"]
  U1 = 74HC595 [package="DIP16 [THT]"]
  7_Segment1 = 7 Segment Display

nets:
  N1: Arduino_Uno.D10_PWM/SS, U1.DS
  N2: Arduino_Uno.D11_PWM/MOSI, U1.ST_CP
  N3: Arduino_Uno.D12/MISO, U1.SH_CP
  GND: Arduino_Uno.GND, R1.Pin_1, U1.GND, U1.OE
  5V: Arduino_Uno.5V, U1.VCC
  N4: R1.Pin_0, 7_Segment1.common_cathode
  N5: U1.Q1, 7_Segment1.Segment_B
  N6: U1.Q2, 7_Segment1.Segment_C
  N7: U1.Q3, 7_Segment1.Segment_D
  N8: U1.Q4, 7_Segment1.Segment_E
  N9: U1.Q5, 7_Segment1.Segment_F
  N10: U1.Q6, 7_Segment1.Segment_A#1
  N11: U1.Q7, 7_Segment1.Segment_DP
  5V_2: U1.MR
  N12: U1.Q0, 7_Segment1.Segment_A#10
