# Fritzing sketch 07_Dot_Matrix (saved by Fritzing 0.9.2b)
breadboards: 1

parts:
  부품1 = Arduino Uno (Rev3) - ICSP
  Disp1 = LBT2088AH [part_number=LBT2088AH]
  U1 = 74HC595 [package="DIP16 [THT]"]

nets:
  GND: 부품1.GND, U1.GND, U1.OE
  5V: 부품1.5V, U1.MR, U1.VCC
  N1: 부품1.D11_PWM/MOSI, U1.SH_CP
  N2: 부품1.D12/MISO, U1.ST_CP
  N3: 부품1.D13/SCK, U1.DS
  N4: 부품1.D0/RX, Disp1.pin_9
  N5: 부품1.D1/TX, Disp1.pin_14
  N6: 부품1.D2, Disp1.pin_8
  N7: 부품1.D3_PWM, Disp1.pin_12
  N8: 부품1.D4, Disp1.pin1
  N9: 부품1.D5_PWM, Disp1.pin_7
  N10: 부품1.D6_PWM, Disp1.pin2
  N11: 부품1.D7, Disp1.pin_5
  N12: Disp1.pin_3, U1.Q1
  N13: Disp1.pin_4, U1.Q2
  N14: Disp1.pin_6, U1.Q4
  N15: Disp1.pin_10, U1.Q3
  N16: Disp1.pin_11, U1.Q5
  N17: Disp1.pin_13, U1.Q0
  N18: Disp1.pin_15, U1.Q6
  N19: Disp1.pin_16, U1.Q7
